# Fritzing sketch telepi-fritzing (saved by Fritzing 0.9.3b)
breadboards: 1

parts:
  J2 = rounded female pin header, 12 pins [form="♀ (female rounded)"]  # not connected
  J3 = rounded female pin header, 12 pins [form="♀ (female rounded)"]  # not connected
  J4 = rounded female pin header, 9 pins [form="♀ (female rounded)"]
  J5 = rounded female pin header, 9 pins [form="♀ (female rounded)"]
  J6 = rounded female pin header, 2 pins [form="♀ (female rounded)"]
  J7 = rounded female pin header, 2 pins [form="♀ (female rounded)"]
  J8 = rounded female pin header, 2 pins [form="♀ (female rounded)"]
  J9 = rounded female pin header, 2 pins [form="♀ (female rounded)"]
  J10 = rounded female pin header, 6 pins [form="♀ (female rounded)"]
  J11 = rounded female pin header, 6 pins [form="♀ (female rounded)"]
  J12 = rounded female pin header, 4 pins [form="♀ (female rounded)"]
  J13 = rounded female pin header, 4 pins [form="♀ (female rounded)"]
  J14 = rounded female pin header, 4 pins [form="♀ (female rounded)"]
  LCD1 = LCD screen  # not connected
  J15 = rounded female pin header, 1 pin [form="♀ (female rounded)"]
  J16 = rounded female pin header, 1 pin [form="♀ (female rounded)"]
  J17 = rounded female pin header, 2 pins [form="♀ (female rounded)"]  # not connected
  J18 = rounded female pin header, 2 pins [form="♀ (female rounded)"]
  J19 = rounded female pin header, 2 pins [form="♀ (female rounded)"]
  J21 = rounded female pin header, 1 pin [form="♀ (female rounded)"]
  J22 = rounded female pin header, 1 pin [form="♀ (female rounded)"]
  J23 = rounded female pin header, 1 pin [form="♀ (female rounded)"]
  J24 = rounded female pin header, 1 pin [form="♀ (female rounded)"]
  J25 = rounded female pin header, 1 pin [form="♀ (female rounded)"]
  J26 = rounded female pin header, 1 pin [form="♀ (female rounded)"]
  J27 = rounded female pin header, 1 pin [form="♀ (female rounded)"]
  J28 = rounded female pin header, 1 pin [form="♀ (female rounded)"]
  J29 = rounded female pin header, 1 pin [form="♀ (female rounded)"]
  J30 = rounded female pin header, 1 pin [form="♀ (female rounded)"]
  J31 = rounded female pin header, 1 pin [form="♀ (female rounded)"]
  R1 = Resistor [tolerance=±5% resistance=390 package=THT]
  R2 = Resistor [tolerance=±5% resistance=390 package=THT]
  R3 = Resistor [tolerance=±5% resistance=390 package=THT]
  R4 = Resistor [tolerance=±5% resistance=390 package=THT]
  R6 = Resistor [tolerance=±5% resistance=10k package=THT]
  R5 = Resistor [tolerance=±5% resistance=10k package=THT]
  R7 = Resistor [tolerance=±5% resistance=4.7k package=THT]
  Composant1 = BME280 Breakout  # not connected

nets:
  N1: J4.pin1, J11.pin1, J13.pin2
  N2: J4.pin2, J11.pin2, J13.pin1
  N3: J4.pin4, J21.pin1, R5.Pin_0
  N4: J5.pin6, J31.pin1
  N5: J5.pin7, J30.pin1
  N6: J5.pin8, J29.pin1
  N7: J5.pin9, J10.pin2, J28.pin1
  N8: J6.pin1, J6.pin2, J14.pin4
  N9: J7.pin1, J7.pin2, J14.pin3
  N10: J8.pin1, J8.pin2, J11.pin6, J12.pin4, J13.pin4, J23.pin1, R1.Pin_1, R2.Pin_1, R3.Pin_1, R4.Pin_1, R6.Pin_1
  N11: J9.pin1, J9.pin2, J11.pin5, J12.pin3, J13.pin3, J19.pin2, R5.Pin_1
  N12: J10.pin4, J14.pin2
  N13: J10.pin5, J14.pin1
  N14: J11.pin3, J12.pin1
  N15: J11.pin4, J12.pin2
  N16: J15.pin1, R7.Pin_1
  N17: J16.pin1, J18.pin2
  N18: J18.pin1, R7.Pin_0
  N19: J19.pin1, J22.pin1, R6.Pin_0
  N20: J24.pin1, R1.Pin_0
  N21: J25.pin1, R2.Pin_0
  N22: J26.pin1, R3.Pin_0
  N23: J27.pin1, R4.Pin_0
